// Logisim project cpu.circ as structural Verilog: 5 circuits, main circuit main
module main (
  input  [31:0] INSTRUCTION,
  input  CLOCK,
  output [31:0] FETCH_ADDRESS,
  output [31:0] s0_Value,
  output [31:0] s1_Value,
  output [31:0] s2_Value,
  output [31:0] ra_Value,
  output [31:0] sp_Value,
  output [31:0] HI_Value,
  output [31:0] LO_Value
);

  Register #(.width(32)) PC ();  // open: D, en, Q, clk, clr
  Register #(.width(32)) LO ();  // open: D, en, Q, clk, clr
  Register #(.width(32)) HI ();  // open: D, en, Q, clk, clr

  // Other names for the same wires on the sheet: clk = CLOCK; fetch_addr[31:0] = FETCH_ADDRESS

  // Notes on the sheet:
  //   Output
  //   Inputs
endmodule

module IFU (
  input  clk,
  output [31:0] instruction
);

  wire [31:0] adder_1_out, PC_q;

  Register #(.width(32)) PC (.D(adder_1_out), .en(1'b1), .Q(PC_q), .clk(clk), .clr(1'b0));
  Adder #(.width(32)) adder_1 (.a(32'h4), .b(PC_q), .out(adder_1_out), .cin(1'b0));  // open: cout
  ROM #(.addrWidth(10), .dataWidth(32)) rom_1 (.addr(PC_q[11:2]), .data(instruction), .sel(1'b1));

  // Notes on the sheet:
  //   /4:word => byte
  //   contents of rom_1 (hex, n*v repeats v):
  //   2538820
endmodule

module RAM (
  input  [31:0] Address,
  input  [31:0] Write_Data,
  input  Write_En,
  input  Clock,
  output [31:0] Read_Data
);

  RAM_part #(.addrWidth(24), .dataWidth(32), .bus("separate")) ram_1 (
    .addr(Address[25:2]), .din(Write_Data), .data(Read_Data), .str(Write_En), .sel(1'b1), .clk(Clock),
    .ld(1'b1), .clr(1'b0));
endmodule

module MIPS (
);

  wire clock_1_out;
  wire [31:0] alu_1_result;

  Clock clock_1 (.out(clock_1_out));
  IFU ifu_1 (.clk(clock_1_out));  // open: instruction
  regfile_main main_1 (
    .Din(alu_1_result), .Clock(clock_1_out));  // open: Reg1_num, Reg2, Write_Reg_num, Write_Enable, Reg1, Reg2_2, s0_Value, s1_Value, s2_Value, ra_Value
  ALU alu_1 (.Result(alu_1_result));  // open: AluOP, X, Equal, Signed_Overflow, Y, Result_2
endmodule

module Decoder (
  input  [31:0] instruction,
  output [25:0] imm26,
  output [15:0] imm16,
  output [5:0] opcode,
  output [4:0] rs,
  output [4:0] rt,
  output [4:0] rd,
  output [4:0] sham,
  output [5:0] funct
);


  assign funct = instruction[5:0];
  assign imm16 = instruction[15:0];
  assign imm26 = instruction[25:0];
  assign opcode = instruction[31:26];
  assign rd = instruction[15:11];
  assign rs = instruction[25:21];
  assign rt = instruction[20:16];
  assign sham = instruction[10:6];

  // Notes on the sheet:
  //   R 型指令译码
  //   I 型指令译码
  //   J 型指令译码
endmodule
